# Fritzing sketch simpleled (saved by Fritzing 0.9.3b)
circuit board: 8.46667cm x 5.64444cm

parts:
  LED1 = smd LED [color="Red (633nm)" package="1206 [SMD]"]
  R1 = Resistor [tolerance=±5% resistance=220 package="2010 [SMD]"]
  BAT1 = Battery Holders [package=battery-aa]

nets:
  N1: LED1.cathode, BAT1.+
  N2: LED1.anode, R1.Pin_0
  N3: R1.Pin_1, BAT1.-
