# Fritzing sketch tftscreenwiring (saved by Fritzing 0.9.3b)
circuit board: 8.46667cm x 5.64444cm
breadboards: 1

parts:
  Part1 = TFT 1.8 inch 160x128 w microSD [part_number=358]
  Part2 = Arduino Uno (Rev3) - ICSP

nets:
  N1: Part1.LITE, Part2.5V
  N2: Part1.MISO, Part2.ICSP_MISO, Part2.D12/MISO
  N3: Part1.SCLK, Part2.D13/SCK
  N4: Part1.MOSI, Part2.D11_PWM/MOSI
  N5: Part1.TFTCS, Part2.D10_PWM/SS
  N6: Part1.CARDCS, Part2.D4
  N7: Part1.TFTDC, Part2.D9_PWM
  N8: Part1.RESET, Part2.D8
  GND: Part1.GND, Part2.GND

custom parts:
  TFT 1.8 inch 160x128 w microSD: This lovely little display breakout is the best way to add a small, colorful and bright display to any project. Since the display uses 4-wire SPI to communicate and has its own pixel-addressable frame buffer, it can be used with every kind of microcontroller. Even a very small one with low memory and few pins available! The 1.8" display has 128x160 color pixels.
